// Logisim project alu.circ as structural Verilog: 1 circuit, main circuit alu
module alu (
  input  [31:0] A,
  input  [31:0] B,
  input  [3:0] ALUSel,
  input  [3:0] in_4,
  input  [3:0] in_5,
  input  [3:0] in_6,
  input  [3:0] in_7,
  output [31:0] Result,
  output [3:0] out_9,
  output [3:0] out_10,
  output [3:0] out_11,
  output [3:0] out_12
);

  wire comparator_1_lt;
  wire [31:0] add0, adder_2_out, and1, bit_extender_1_out, bit_extender_2_out, divu8, mul10, mulh14, mulhu11,
       multiplier_1_cout, multiplier_3_out, multiplier_4_out, or2, remu9, sll6, slt7, sra5, srl4, sub12, xor3;

  assign bit_extender_1_out = {{31{A[31]}}, A[31]};  // Bit_Extender bit_extender_1
  assign bit_extender_2_out = {{31{B[31]}}, B[31]};  // Bit_Extender bit_extender_2
  Multiplier #(.width(32)) multiplier_1 (.a(A), .b(B), .cout(multiplier_1_cout));  // open: out, cin
  Adder #(.width(32)) adder_1 (.a(A), .b(B), .out(add0));  // open: cin, cout
  assign and1 = A & B;  // AND_Gate and_1, 32 bits wide
  assign or2 = A | B;  // OR_Gate or_1, 32 bits wide
  assign xor3 = A ^ B;  // XOR_Gate xor_1, 32 bits wide
  Shifter #(.width(32), .shift("lr")) shifter_1 (.in(A), .\dist (B[4:0]), .out(srl4));
  Shifter #(.width(32), .shift("ar")) shifter_2 (.in(A), .\dist (B[4:0]), .out(sra5));
  Shifter #(.width(32)) shifter_3 (.in(A), .\dist (B[4:0]), .out(sll6));
  Comparator #(.width(32)) comparator_1 (.a(A), .b(B), .lt(comparator_1_lt));  // open: gt, eq
  Divider #(.width(32)) divider_1 (.a(A), .b(B), .out(divu8), .rem(remu9));  // open: upper
  Multiplier #(.width(32)) multiplier_2 (.a(A), .b(B), .out(mul10), .cout(mulhu11));  // open: cin
  Subtractor #(.width(32)) subtractor_1 (.a(A), .b(B), .out(sub12));  // open: bin, bout
  Multiplier #(.width(32)) multiplier_3 (.a(bit_extender_1_out), .b(B), .out(multiplier_3_out));  // open: cin, cout
  Multiplier #(.width(32)) multiplier_4 (.a(A), .b(bit_extender_2_out), .out(multiplier_4_out));  // open: cin, cout
  assign slt7 = {{31{1'b0}}, comparator_1_lt};  // Bit_Extender bit_extender_3
  Adder #(.width(32)) adder_2 (.a(multiplier_3_out), .b(multiplier_4_out), .out(adder_2_out));  // open: cin, cout
  Adder #(.width(32)) adder_3 (.a(adder_2_out), .b(multiplier_1_cout), .out(mulh14));  // open: cin, cout
  Multiplexer #(.select(4), .width(32), .enable("false")) multiplexer_1 (
    .in0(add0), .in1(and1), .in2(or2), .in3(xor3), .in4(srl4), .in5(sra5), .in6(sll6), .in7(slt7),
    .in8(divu8), .in9(remu9), .in10(mul10), .in11(mulhu11), .in12(sub12), .in13(B), .in14(mulh14),
    .out(Result), .sel(ALUSel));  // open: in15
  Multiplier #(.width(4)) multiplier_5 (.a(in_4), .b(in_5), .out(out_9), .cout(out_10));  // open: cin
  Divider #(.width(4)) divider_2 (.a(in_6), .b(in_7), .out(out_11), .rem(out_12));  // open: upper

  // Other names for the same wires on the sheet: bsel13[31:0] = B

  // Notes on the sheet:
  //   INPUTS to your circuit
  //   DON'T CHANGE THE LOCATIONS OF THE INPUTS AND OUTPUTS!
  //   OUTPUT from your circuit
endmodule
