// Logisim project control_logic.circ as structural Verilog: 1 circuit, main circuit control_logic
module control_logic (
  input  [31:0] inst,
  input  BrEq,
  input  BrLt,
  output PCSel,
  output RegWEn,
  output [2:0] ImmSel,
  output BrUn,
  output ASel,
  output BSel,
  output [3:0] ALUSel,
  output MemRW,
  output [1:0] WBSel
);

  wire ALU0, ALU1, ALU2, ALU3, ALU4, ALU5, ALU6, ALU7, ALU8, ALU9, ALU10, ALU11, ALU12, ALU13, ALU14,
       and_1_out, and_3_out, and_4_out, and_5_out, and_6_out, and_7_out, and_8_out, and_9_out, and_10_out,
       and_11_out, and_12_out, and_13_out, and_14_out, and_15_out, and_16_out, and_17_out, and_18_out,
       and_19_out, BrUn1, comparator_1_eq, comparator_2_eq, comparator_3_eq, comparator_4_eq,
       comparator_5_eq, comparator_6_eq, comparator_7_eq, comparator_8_eq, comparator_9_eq, comparator_10_eq,
       comparator_11_eq, comparator_12_eq, comparator_13_eq, comparator_14_eq, comparator_15_eq,
       comparator_16_eq, comparator_17_eq, comparator_18_eq, comparator_19_eq, comparator_20_eq,
       comparator_21_eq, comparator_22_eq, comparator_23_eq, comparator_24_eq, comparator_25_eq,
       comparator_27_eq, comparator_28_eq, comparator_29_eq, comparator_30_eq, comparator_31_eq,
       comparator_32_eq, comparator_33_eq, comparator_34_eq, comparator_35_eq, comparator_36_eq,
       comparator_37_eq, comparator_38_eq, comparator_39_eq, comparator_40_eq, comparator_41_eq,
       comparator_42_eq, comparator_43_eq, comparator_44_eq, comparator_45_eq, comparator_46_eq,
       comparator_47_eq, comparator_48_eq, comparator_49_eq, comparator_50_eq, comparator_51_eq,
       comparator_52_eq, comparator_53_eq, comparator_54_eq, comparator_55_eq, comparator_56_eq,
       comparator_57_eq, comparator_58_eq, comparator_59_eq, comparator_60_eq, comparator_61_eq,
       comparator_62_eq, comparator_63_eq, comparator_64_eq, comparator_65_eq, comparator_66_eq,
       comparator_67_eq, comparator_68_eq, comparator_69_eq, comparator_70_eq, comparator_71_eq,
       comparator_72_eq, comparator_73_eq, comparator_74_eq, comparator_75_eq, comparator_76_eq,
       comparator_77_eq, comparator_78_eq, comparator_79_eq, comparator_80_eq, comparator_81_eq,
       comparator_82_eq, comparator_83_eq, comparator_84_eq, comparator_85_eq, comparator_86_eq,
       comparator_87_eq, comparator_88_eq, comparator_89_eq, comparator_90_eq, comparator_91_eq,
       comparator_92_eq, comparator_93_eq, comparator_94_eq, comparator_95_eq, comparator_96_eq,
       comparator_97_eq, comparator_98_eq, comparator_100_eq, comparator_101_eq, comparator_102_eq,
       multiplexer_1_out, not_1_out, not_2_out, or_1_out, or_2_out, or_3_out, or_5_out, or_6_out, or_8_out;

  Comparator #(.width(7)) comparator_1 (.a(7'b1100011), .b(inst[6:0]), .eq(comparator_1_eq));  // open: gt, lt
  not not_1 (not_1_out, BrEq);
  not not_2 (not_2_out, BrLt);
  Comparator #(.width(7)) comparator_2 (.a(7'b1100111), .b(inst[6:0]), .eq(comparator_2_eq));  // open: gt, lt
  Comparator #(.width(7)) comparator_3 (.a(7'b0000011), .b(inst[6:0]), .eq(comparator_3_eq));  // open: gt, lt
  Comparator #(.width(7)) comparator_4 (.a(7'b0010011), .b(inst[6:0]), .eq(comparator_4_eq));  // open: gt, lt
  Comparator #(.width(7)) comparator_5 (.a(7'b0100011), .b(inst[6:0]), .eq(comparator_5_eq));  // open: gt, lt
  Comparator #(.width(7)) comparator_6 (.a(7'b1100011), .b(inst[6:0]), .eq(comparator_6_eq));  // open: gt, lt
  Comparator #(.width(7)) comparator_7 (.a(7'b0010111), .b(inst[6:0]), .eq(comparator_7_eq));  // open: gt, lt
  Comparator #(.width(7)) comparator_8 (.a(7'b0110111), .b(inst[6:0]), .eq(comparator_8_eq));  // open: gt, lt
  Comparator #(.width(7)) comparator_9 (.a(7'b1101111), .b(inst[6:0]), .eq(comparator_9_eq));  // open: gt, lt
  Comparator #(.width(7)) comparator_10 (.a(inst[6:0]), .b(7'b0110011), .eq(comparator_10_eq));  // open: gt, lt
  Comparator #(.width(7)) comparator_11 (.a(inst[6:0]), .b(7'b0000011), .eq(comparator_11_eq));  // open: gt, lt
  Comparator #(.width(7)) comparator_12 (.a(inst[6:0]), .b(7'b0010011), .eq(comparator_12_eq));  // open: gt, lt
  Comparator #(.width(7)) comparator_13 (.a(inst[6:0]), .b(7'b0010111), .eq(comparator_13_eq));  // open: gt, lt
  Comparator #(.width(7)) comparator_14 (.a(inst[6:0]), .b(7'b0110111), .eq(comparator_14_eq));  // open: gt, lt
  Comparator #(.width(7)) comparator_15 (.a(inst[6:0]), .b(7'b1101111), .eq(comparator_15_eq));  // open: gt, lt
  Comparator #(.width(7)) comparator_16 (.a(inst[6:0]), .b(7'b1100111), .eq(comparator_16_eq));  // open: gt, lt
  Comparator #(.width(7)) comparator_17 (.a(inst[6:0]), .b(7'b0000011), .eq(comparator_17_eq));  // open: gt, lt
  Comparator #(.width(7)) comparator_18 (.a(inst[6:0]), .b(7'b0010111), .eq(comparator_18_eq));  // open: gt, lt
  Comparator #(.width(7)) comparator_19 (.a(inst[6:0]), .b(7'b0110111), .eq(comparator_19_eq));  // open: gt, lt
  Comparator #(.width(7)) comparator_20 (.a(inst[6:0]), .b(7'b0010011), .eq(comparator_20_eq));  // open: gt, lt
  Comparator #(.width(7)) comparator_21 (.a(inst[6:0]), .b(7'b0110011), .eq(comparator_21_eq));  // open: gt, lt
  Comparator #(.width(7)) comparator_22 (.a(inst[6:0]), .b(7'b1101111), .eq(comparator_22_eq));  // open: gt, lt
  Comparator #(.width(7)) comparator_23 (.a(inst[6:0]), .b(7'b1100111), .eq(comparator_23_eq));  // open: gt, lt
  Comparator #(.width(7)) comparator_24 (.a(7'b1100111), .b(inst[6:0]), .eq(comparator_24_eq));  // open: gt, lt
  Comparator #(.width(7)) comparator_25 (.a(7'b1101111), .b(inst[6:0]), .eq(comparator_25_eq));  // open: gt, lt
  Multiplexer #(.select(2), .enable("false")) multiplexer_1 (
    .in0(BrEq), .in1(not_1_out), .in2(BrLt), .in3(not_2_out), .out(multiplexer_1_out),
    .sel({inst[14], inst[12]}));
  Comparator #(.width(7)) comparator_26 (.a(inst[6:0]), .b(7'b0100011), .eq(MemRW));  // open: gt, lt
  or or_1 (or_1_out, comparator_18_eq, comparator_19_eq, comparator_20_eq, comparator_21_eq);
  or or_2 (or_2_out, comparator_22_eq, comparator_23_eq);
  or or_3 (or_3_out, comparator_24_eq, comparator_25_eq);
  or or_4 (PCSel, or_3_out, and_1_out);
  and and_1 (and_1_out, comparator_1_eq, multiplexer_1_out);
  or or_5 (or_5_out, comparator_2_eq, comparator_3_eq, comparator_4_eq);
  or or_6 (or_6_out, comparator_7_eq, comparator_8_eq);
  or or_7 (RegWEn, comparator_10_eq, comparator_11_eq, comparator_12_eq, comparator_13_eq, comparator_14_eq, comparator_15_eq, comparator_16_eq);
  Priority_Encoder #(.select(2)) priority_encoder_1 (
    .in0(comparator_17_eq), .in1(or_1_out), .in2(or_2_out), .out(WBSel));  // open: in3, gs, en_out, en_in
  Priority_Encoder priority_encoder_2 (
    .in0(or_5_out), .in1(comparator_5_eq), .in2(comparator_6_eq), .in3(or_6_out), .in4(comparator_9_eq),
    .out(ImmSel));  // open: in5, in6, in7, en_in, gs, en_out
  Comparator #(.width(7)) comparator_27 (.a(7'b1100011), .b(inst[6:0]), .eq(comparator_27_eq));  // open: gt, lt
  Comparator #(.width(3)) comparator_28 (.a(3'b110), .b(inst[14:12]), .eq(comparator_28_eq));  // open: gt, lt
  Comparator #(.width(3)) comparator_29 (.a(3'b111), .b(inst[14:12]), .eq(comparator_29_eq));  // open: gt, lt
  Comparator #(.width(7)) comparator_30 (.a(7'b1100011), .b(inst[6:0]), .eq(comparator_30_eq));  // open: gt, lt
  Comparator #(.width(7)) comparator_31 (.a(7'b0010111), .b(inst[6:0]), .eq(comparator_31_eq));  // open: gt, lt
  Comparator #(.width(7)) comparator_32 (.a(7'b1101111), .b(inst[6:0]), .eq(comparator_32_eq));  // open: gt, lt
  Comparator #(.width(7)) comparator_33 (.a(7'b0110011), .b(inst[6:0]), .eq(comparator_33_eq));  // open: gt, lt
  or or_8 (or_8_out, comparator_28_eq, comparator_29_eq);
  or or_9 (ASel, comparator_30_eq, comparator_31_eq, comparator_32_eq);
  not not_3 (BSel, comparator_33_eq);
  and and_2 (BrUn1, comparator_27_eq, or_8_out);
  Comparator #(.width(7)) comparator_34 (.a(7'b0100011), .b(inst[6:0]), .eq(comparator_34_eq));  // open: gt, lt
  Comparator #(.width(3)) comparator_35 (.a(3'b010), .b(inst[14:12]), .eq(comparator_35_eq));  // open: gt, lt
  Comparator #(.width(7)) comparator_36 (.a(7'b0110011), .b(inst[6:0]), .eq(comparator_36_eq));  // open: gt, lt
  Comparator #(.width(3)) comparator_37 (.a(3'b000), .b(inst[14:12]), .eq(comparator_37_eq));  // open: gt, lt
  Comparator #(.width(7)) comparator_38 (.a({7{1'b0}}), .b(inst[31:25]), .eq(comparator_38_eq));  // open: gt, lt
  Comparator #(.width(7)) comparator_39 (.a(7'b0000011), .b(inst[6:0]), .eq(comparator_39_eq));  // open: gt, lt
  Comparator #(.width(7)) comparator_40 (.a(7'b0010011), .b(inst[6:0]), .eq(comparator_40_eq));  // open: gt, lt
  Comparator #(.width(3)) comparator_41 (.a(3'b000), .b(inst[14:12]), .eq(comparator_41_eq));  // open: gt, lt
  Comparator #(.width(7)) comparator_42 (.a(7'b1100011), .b(inst[6:0]), .eq(comparator_42_eq));  // open: gt, lt
  Comparator #(.width(7)) comparator_43 (.a(7'b0010111), .b(inst[6:0]), .eq(comparator_43_eq));  // open: gt, lt
  Comparator #(.width(7)) comparator_44 (.a(7'b1101111), .b(inst[6:0]), .eq(comparator_44_eq));  // open: gt, lt
  Comparator #(.width(7)) comparator_45 (.a(7'b1100111), .b(inst[6:0]), .eq(comparator_45_eq));  // open: gt, lt
  Comparator #(.width(7)) comparator_46 (.a(7'b0110011), .b(inst[6:0]), .eq(comparator_46_eq));  // open: gt, lt
  Comparator #(.width(3)) comparator_47 (.a(3'b111), .b(inst[14:12]), .eq(comparator_47_eq));  // open: gt, lt
  Comparator #(.width(7)) comparator_48 (.a({7{1'b0}}), .b(inst[31:25]), .eq(comparator_48_eq));  // open: gt, lt
  Comparator #(.width(7)) comparator_49 (.a(7'b0010011), .b(inst[6:0]), .eq(comparator_49_eq));  // open: gt, lt
  Comparator #(.width(3)) comparator_50 (.a(3'b111), .b(inst[14:12]), .eq(comparator_50_eq));  // open: gt, lt
  Comparator #(.width(7)) comparator_51 (.a(7'b0110011), .b(inst[6:0]), .eq(comparator_51_eq));  // open: gt, lt
  Comparator #(.width(3)) comparator_52 (.a(3'b110), .b(inst[14:12]), .eq(comparator_52_eq));  // open: gt, lt
  Comparator #(.width(7)) comparator_53 (.a({7{1'b0}}), .b(inst[31:25]), .eq(comparator_53_eq));  // open: gt, lt
  Comparator #(.width(7)) comparator_54 (.a(7'b0010011), .b(inst[6:0]), .eq(comparator_54_eq));  // open: gt, lt
  Comparator #(.width(3)) comparator_55 (.a(3'b110), .b(inst[14:12]), .eq(comparator_55_eq));  // open: gt, lt
  Comparator #(.width(7)) comparator_56 (.a(7'b0110011), .b(inst[6:0]), .eq(comparator_56_eq));  // open: gt, lt
  Comparator #(.width(3)) comparator_57 (.a(3'b100), .b(inst[14:12]), .eq(comparator_57_eq));  // open: gt, lt
  Comparator #(.width(7)) comparator_58 (.a({7{1'b0}}), .b(inst[31:25]), .eq(comparator_58_eq));  // open: gt, lt
  Comparator #(.width(7)) comparator_59 (.a(7'b0010011), .b(inst[6:0]), .eq(comparator_59_eq));  // open: gt, lt
  Comparator #(.width(3)) comparator_60 (.a(3'b100), .b(inst[14:12]), .eq(comparator_60_eq));  // open: gt, lt
  Comparator #(.width(7)) comparator_61 (.a(7'b0110011), .b(inst[6:0]), .eq(comparator_61_eq));  // open: gt, lt
  Comparator #(.width(3)) comparator_62 (.a(3'b101), .b(inst[14:12]), .eq(comparator_62_eq));  // open: gt, lt
  Comparator #(.width(7)) comparator_63 (.a({7{1'b0}}), .b(inst[31:25]), .eq(comparator_63_eq));  // open: gt, lt
  Comparator #(.width(7)) comparator_64 (.a(7'b0010011), .b(inst[6:0]), .eq(comparator_64_eq));  // open: gt, lt
  Comparator #(.width(3)) comparator_65 (.a(3'b101), .b(inst[14:12]), .eq(comparator_65_eq));  // open: gt, lt
  Comparator #(.width(7)) comparator_66 (.a({7{1'b0}}), .b(inst[31:25]), .eq(comparator_66_eq));  // open: gt, lt
  Comparator #(.width(7)) comparator_67 (.a(7'b0110011), .b(inst[6:0]), .eq(comparator_67_eq));  // open: gt, lt
  Comparator #(.width(3)) comparator_68 (.a(3'b101), .b(inst[14:12]), .eq(comparator_68_eq));  // open: gt, lt
  Comparator #(.width(7)) comparator_69 (.a(7'b0100000), .b(inst[31:25]), .eq(comparator_69_eq));  // open: gt, lt
  Comparator #(.width(7)) comparator_70 (.a(7'b0010011), .b(inst[6:0]), .eq(comparator_70_eq));  // open: gt, lt
  Comparator #(.width(3)) comparator_71 (.a(3'b101), .b(inst[14:12]), .eq(comparator_71_eq));  // open: gt, lt
  Comparator #(.width(7)) comparator_72 (.a(7'b0100000), .b(inst[31:25]), .eq(comparator_72_eq));  // open: gt, lt
  Comparator #(.width(7)) comparator_73 (.a(7'b0110011), .b(inst[6:0]), .eq(comparator_73_eq));  // open: gt, lt
  Comparator #(.width(3)) comparator_74 (.a(3'b001), .b(inst[14:12]), .eq(comparator_74_eq));  // open: gt, lt
  Comparator #(.width(7)) comparator_75 (.a({7{1'b0}}), .b(inst[31:25]), .eq(comparator_75_eq));  // open: gt, lt
  Comparator #(.width(7)) comparator_76 (.a(7'b0010011), .b(inst[6:0]), .eq(comparator_76_eq));  // open: gt, lt
  Comparator #(.width(3)) comparator_77 (.a(3'b001), .b(inst[14:12]), .eq(comparator_77_eq));  // open: gt, lt
  Comparator #(.width(7)) comparator_78 (.a({7{1'b0}}), .b(inst[31:25]), .eq(comparator_78_eq));  // open: gt, lt
  Comparator #(.width(7)) comparator_79 (.a(7'b0110011), .b(inst[6:0]), .eq(comparator_79_eq));  // open: gt, lt
  Comparator #(.width(3)) comparator_80 (.a(3'b010), .b(inst[14:12]), .eq(comparator_80_eq));  // open: gt, lt
  Comparator #(.width(7)) comparator_81 (.a({7{1'b0}}), .b(inst[31:25]), .eq(comparator_81_eq));  // open: gt, lt
  Comparator #(.width(7)) comparator_82 (.a(7'b0010011), .b(inst[6:0]), .eq(comparator_82_eq));  // open: gt, lt
  Comparator #(.width(3)) comparator_83 (.a(3'b010), .b(inst[14:12]), .eq(comparator_83_eq));  // open: gt, lt
  Comparator #(.width(7)) comparator_84 (.a(7'b0110011), .b(inst[6:0]), .eq(comparator_84_eq));  // open: gt, lt
  Comparator #(.width(3)) comparator_85 (.a(3'b101), .b(inst[14:12]), .eq(comparator_85_eq));  // open: gt, lt
  Comparator #(.width(7)) comparator_86 (.a(7'b0000001), .b(inst[31:25]), .eq(comparator_86_eq));  // open: gt, lt
  Comparator #(.width(7)) comparator_87 (.a(7'b0110011), .b(inst[6:0]), .eq(comparator_87_eq));  // open: gt, lt
  Comparator #(.width(3)) comparator_88 (.a(3'b111), .b(inst[14:12]), .eq(comparator_88_eq));  // open: gt, lt
  Comparator #(.width(7)) comparator_89 (.a(7'b0000001), .b(inst[31:25]), .eq(comparator_89_eq));  // open: gt, lt
  Comparator #(.width(7)) comparator_90 (.a(7'b0110011), .b(inst[6:0]), .eq(comparator_90_eq));  // open: gt, lt
  Comparator #(.width(3)) comparator_91 (.a(3'b000), .b(inst[14:12]), .eq(comparator_91_eq));  // open: gt, lt
  Comparator #(.width(7)) comparator_92 (.a(7'b0000001), .b(inst[31:25]), .eq(comparator_92_eq));  // open: gt, lt
  Comparator #(.width(7)) comparator_93 (.a(7'b0110011), .b(inst[6:0]), .eq(comparator_93_eq));  // open: gt, lt
  Comparator #(.width(3)) comparator_94 (.a(3'b011), .b(inst[14:12]), .eq(comparator_94_eq));  // open: gt, lt
  Comparator #(.width(7)) comparator_95 (.a(7'b0000001), .b(inst[31:25]), .eq(comparator_95_eq));  // open: gt, lt
  Comparator #(.width(7)) comparator_96 (.a(7'b0110011), .b(inst[6:0]), .eq(comparator_96_eq));  // open: gt, lt
  Comparator #(.width(3)) comparator_97 (.a(3'b000), .b(inst[14:12]), .eq(comparator_97_eq));  // open: gt, lt
  Comparator #(.width(7)) comparator_98 (.a(7'b0100000), .b(inst[31:25]), .eq(comparator_98_eq));  // open: gt, lt
  Comparator #(.width(7)) comparator_99 (.a(7'b0110111), .b(inst[6:0]), .eq(ALU13));  // open: gt, lt
  Comparator #(.width(7)) comparator_100 (.a(7'b0110011), .b(inst[6:0]), .eq(comparator_100_eq));  // open: gt, lt
  Comparator #(.width(3)) comparator_101 (.a(3'b001), .b(inst[14:12]), .eq(comparator_101_eq));  // open: gt, lt
  Comparator #(.width(7)) comparator_102 (.a(7'b0000001), .b(inst[31:25]), .eq(comparator_102_eq));  // open: gt, lt
  and and_3 (and_3_out, comparator_34_eq, comparator_35_eq);
  and and_4 (and_4_out, comparator_36_eq, comparator_37_eq, comparator_38_eq);
  and and_5 (and_5_out, comparator_40_eq, comparator_41_eq);
  and and_6 (and_6_out, comparator_46_eq, comparator_47_eq, comparator_48_eq);
  and and_7 (and_7_out, comparator_49_eq, comparator_50_eq);
  and and_8 (and_8_out, comparator_51_eq, comparator_52_eq, comparator_53_eq);
  and and_9 (and_9_out, comparator_54_eq, comparator_55_eq);
  and and_10 (and_10_out, comparator_56_eq, comparator_57_eq, comparator_58_eq);
  and and_11 (and_11_out, comparator_59_eq, comparator_60_eq);
  and and_12 (and_12_out, comparator_61_eq, comparator_62_eq, comparator_63_eq);
  and and_13 (and_13_out, comparator_64_eq, comparator_65_eq, comparator_66_eq);
  and and_14 (and_14_out, comparator_67_eq, comparator_68_eq, comparator_69_eq);
  and and_15 (and_15_out, comparator_70_eq, comparator_71_eq, comparator_72_eq);
  and and_16 (and_16_out, comparator_73_eq, comparator_74_eq, comparator_75_eq);
  and and_17 (and_17_out, comparator_76_eq, comparator_77_eq, comparator_78_eq);
  and and_18 (and_18_out, comparator_79_eq, comparator_80_eq, comparator_81_eq);
  and and_19 (and_19_out, comparator_82_eq, comparator_83_eq);
  and and_20 (ALU8, comparator_84_eq, comparator_85_eq, comparator_86_eq);
  and and_21 (ALU9, comparator_87_eq, comparator_88_eq, comparator_89_eq);
  and and_22 (ALU10, comparator_90_eq, comparator_91_eq, comparator_92_eq);
  and and_23 (ALU11, comparator_93_eq, comparator_94_eq, comparator_95_eq);
  and and_24 (ALU12, comparator_96_eq, comparator_97_eq, comparator_98_eq);
  and and_25 (ALU14, comparator_100_eq, comparator_101_eq, comparator_102_eq);
  or or_10 (ALU1, and_6_out, and_7_out);
  or or_11 (ALU2, and_8_out, and_9_out);
  or or_12 (ALU3, and_10_out, and_11_out);
  or or_13 (ALU4, and_12_out, and_13_out);
  or or_14 (ALU5, and_14_out, and_15_out);
  or or_15 (ALU6, and_16_out, and_17_out);
  or or_16 (ALU7, and_18_out, and_19_out);
  or or_17 (ALU0, and_3_out, and_4_out, comparator_39_eq, and_5_out, comparator_43_eq, comparator_44_eq, comparator_45_eq, comparator_42_eq);
  Priority_Encoder #(.select(4)) priority_encoder_3 (
    .in0(ALU0), .in1(ALU1), .in2(ALU2), .in3(ALU3), .in4(ALU4), .in5(ALU5), .in6(ALU6), .in7(ALU7),
    .in8(ALU8), .in9(ALU9), .in10(ALU10), .in11(ALU11), .in12(ALU12), .in13(ALU13), .in14(ALU14), .out(ALUSel));  // open: in15, gs, en_out, en_in

  assign BrUn = inst[13];

  // Other names for the same wires on the sheet: Opcode[6:0] = inst[6:0]; funct3[2:0] = inst[14:12];
  //   funct7[6:0] = inst[31:25]

  // Notes on the sheet:
  //   INPUTS to your circuit
  //   DON'T CHANGE THE LOCATIONS OF THE INPUTS AND OUTPUTS!
  //   OUTPUT from your circuit
  //   reference on github.com/uning/CS61C-SU21-proj3 
endmodule
