// Logisim project cpu copy.circ as structural Verilog: 1 circuit, main circuit main
module main (
  input  [31:0] INSTRUCTION,
  input  CLOCK,
  output [31:0] PROGRAM_COUNTER,
  output [31:0] ra,
  output [31:0] sp,
  output [31:0] t0,
  output [31:0] t1,
  output [31:0] t2,
  output [31:0] s0,
  output [31:0] s1,
  output [31:0] a0
);

  wire ASel, BrEq, BrLt, BrUn, BSel, MemRW, PCSel, RegWEn;
  wire [1:0] WBSel;
  wire [2:0] funct3, ImmSel;
  wire [3:0] ALUSel;
  wire [6:0] func7;
  wire [24:0] INSTRUCTION_AfterReg;
  wire [31:0] adder_1_out, adder_2_out, ALU_output, DMEM_ReadData, immediate, multiplexer_1_out,
       multiplexer_2_out, multiplexer_3_out, multiplexer_4_out, PC_AfterReg, rs1_output, rs2_output, WBValue;

  Adder #(.width(32)) adder_1 (.a(PROGRAM_COUNTER), .b(32'h4), .out(adder_1_out));  // open: cin, cout
  Multiplexer #(.width(32), .enable("false")) multiplexer_1 (
    .in0(INSTRUCTION), .in1(32'h13), .out(multiplexer_1_out), .sel(PCSel));
  control_logic control_logic_1 (
    .BSel(BSel), .RegWEn(RegWEn), .ASel(ASel), .ImmSel(ImmSel), .BrUn(BrUn), .PCSel(PCSel), .BrLt(BrLt),
    .BrEq(BrEq), .inst({func7, INSTRUCTION_AfterReg[24:15], funct3, INSTRUCTION_AfterReg[11:0]}),
    .ALUSel(ALUSel), .MemRW(MemRW), .WBSel(WBSel));
  Multiplexer #(.width(32), .enable("false")) multiplexer_2 (
    .in0(adder_1_out), .in1(ALU_output), .out(multiplexer_2_out), .sel(PCSel));
  Register #(.width(32)) register_1 (.D(PROGRAM_COUNTER), .clk(CLOCK), .Q(PC_AfterReg));  // open: en, clr
  Register #(.width(32)) PC (.D(multiplexer_2_out), .clk(CLOCK), .Q(PROGRAM_COUNTER));  // open: en, clr
  Register #(.width(32)) register_2 (
    .D(multiplexer_1_out), .clk(CLOCK),
    .Q({func7, INSTRUCTION_AfterReg[24:15], funct3, INSTRUCTION_AfterReg[11:0]}));  // open: en, clr
  imm_gen imm_gen_1 (
    .ImmSel(ImmSel), .inst({func7, INSTRUCTION_AfterReg[24:15], funct3, INSTRUCTION_AfterReg[11:0]}),
    .imm(immediate));
  branch_comp branch_comp_1 (.BrEq(BrEq), .BrUn(BrUn), .rs1(rs1_output), .BrLt(BrLt), .rs2(rs2_output));
  regfile_main RegFile (
    .rs2(INSTRUCTION_AfterReg[24:20]), .rd(INSTRUCTION_AfterReg[11:7]), .Read_Data_1(rs1_output),
    .Read_Data_2(rs2_output), .ra(ra), .sp(sp), .t0(t0), .t1(t1), .t2(t2), .s0(s0), .s1(s1), .a0(a0),
    .rs1(INSTRUCTION_AfterReg[19:15]), .Write_Data(WBValue), .RegWEn(RegWEn), .clk(CLOCK));  // open: out_19, out_20, in_7, in_8
  Multiplexer #(.width(32), .enable("false")) multiplexer_3 (
    .in0(rs1_output), .in1(PC_AfterReg), .out(multiplexer_3_out), .sel(ASel));
  Multiplexer #(.width(32), .enable("false")) multiplexer_4 (
    .in0(rs2_output), .in1(immediate), .out(multiplexer_4_out), .sel(BSel));
  alu Arithmetic_Logic_Unit (
    .ALUSel(ALUSel), .Result(ALU_output), .A(multiplexer_3_out), .B(multiplexer_4_out));  // open: in_4, in_5, out_9, out_10, in_6, in_7, out_11, out_12
  Adder #(.width(32)) adder_2 (.a(PC_AfterReg), .b(32'h4), .out(adder_2_out));  // open: cin, cout
  // mem_main DMEM: pin names not known; wires that end beside it: ALU_output, rs2_output, CLOCK, MemRW, DMEM_ReadData
  Multiplexer #(.select(2), .width(32), .enable("false")) multiplexer_5 (
    .in0(DMEM_ReadData), .in1(ALU_output), .in2(adder_2_out), .out(WBValue), .sel(WBSel));  // open: in3

  // Other names for the same wires on the sheet: clk = CLOCK; opcode[6:0] = INSTRUCTION_AfterReg[6:0];
  //   rd[4:0] = INSTRUCTION_AfterReg[11:7]; INSTRUCTION_AfterReg (some bits) = {func7, funct3};
  //   rs1_input[4:0] = INSTRUCTION_AfterReg[19:15]; rs2_input[4:0] = INSTRUCTION_AfterReg[24:20]

  // Notes on the sheet:
  //   Output
  //   IMEM (do **NOT** move this)
  //   Inputs
  //   It is OK to move the PC, RegFile, ALU, MEM, Branch Comp, Imm Gen, and Control Logic to wherever is most convenient for you when constructing your CPU, and to delete this text
  //   Inputs/Outputs for testing. Do **NOT** move these.
endmodule
