// Logisim project cpu.circ as structural Verilog: 1 circuit, main circuit main
module main (
  input  [31:0] INSTRUCTION,
  input  CLOCK,
  output [31:0] PROGRAM_COUNTER,
  output [31:0] ra,
  output [31:0] sp,
  output [31:0] t0,
  output [31:0] t1,
  output [31:0] t2,
  output [31:0] s0,
  output [31:0] s1,
  output [31:0] a0,
  output [31:0] out_12
);

  wire ASel, BrEq, BrLt, BrUn, BSel, MemRW, PCSel, RegWEn;
  wire [1:0] bit_extender_1_out, bit_extender_2_out, WBSel;
  wire [2:0] ImmSel;
  wire [3:0] ALUSel;
  wire [7:0] multiplexer_5_out;
  wire [15:0] multiplexer_6_out;
  wire [31:0] adder_1_out, adder_2_out, ALU_output, bit_extender_3_out, bit_extender_4_out, immediate,
       INSTRUCTION_AfterReg, multiplexer_1_out, multiplexer_2_out, multiplexer_3_out, multiplexer_4_out,
       multiplexer_8_out, PC_AfterReg, RegFile_read_data_1, RegFile_read_data_2, WBValue;

  Adder #(.width(32)) adder_1 (.a(PROGRAM_COUNTER), .b(32'h4), .out(adder_1_out));  // open: cin, cout
  Multiplexer #(.width(32), .enable("false")) multiplexer_1 (
    .in0(INSTRUCTION), .in1(32'h13), .out(multiplexer_1_out), .sel(PCSel));
  Multiplexer #(.width(32), .enable("false")) multiplexer_2 (
    .in0(adder_1_out), .in1(ALU_output), .out(multiplexer_2_out), .sel(PCSel));
  control_logic control_logic_1 (
    .BSel(BSel), .RegWEn(RegWEn), .ASel(ASel), .ImmSel(ImmSel), .BrUn(BrUn), .PCSel(PCSel), .BrLt(BrLt),
    .BrEq(BrEq), .inst(INSTRUCTION_AfterReg), .ALUSel(ALUSel), .MemRW(MemRW), .WBSel(WBSel));
  Register #(.width(32)) PC (.D(multiplexer_2_out), .clk(CLOCK), .Q(PROGRAM_COUNTER));  // open: en, clr
  Register #(.width(32)) register_1 (.D(multiplexer_1_out), .clk(CLOCK), .Q(INSTRUCTION_AfterReg));  // open: en, clr
  Register #(.width(32)) register_2 (.D(PROGRAM_COUNTER), .clk(CLOCK), .Q(PC_AfterReg));  // open: en, clr
  imm_gen imm_gen_1 (.ImmSel(ImmSel), .inst(INSTRUCTION_AfterReg), .imm(immediate));
  regfile_main RegFile (
    .rs2(INSTRUCTION_AfterReg[24:20]), .rd(INSTRUCTION_AfterReg[11:7]), .Read_Data_1(RegFile_read_data_1),
    .Read_Data_2(RegFile_read_data_2), .ra(ra), .sp(sp), .t0(t0), .t1(t1), .t2(t2), .s0(s0), .s1(s1),
    .a0(a0), .rs1(INSTRUCTION_AfterReg[19:15]), .Write_Data(WBValue), .RegWEn(RegWEn), .clk(CLOCK));  // open: out_19, out_20, in_7, in_8
  branch_comp branch_comp_1 (
    .BrEq(BrEq), .BrUn(BrUn), .rs1(RegFile_read_data_1), .BrLt(BrLt), .rs2(RegFile_read_data_2));
  Multiplexer #(.width(32), .enable("false")) multiplexer_3 (
    .in0(RegFile_read_data_1), .in1(PC_AfterReg), .out(multiplexer_3_out), .sel(ASel));
  Multiplexer #(.width(32), .enable("false")) multiplexer_4 (
    .in0(RegFile_read_data_2), .in1(immediate), .out(multiplexer_4_out), .sel(BSel));
  alu Arithmetic_Logic_Unit (
    .ALUSel(ALUSel), .Result(ALU_output), .A(multiplexer_3_out), .B(multiplexer_4_out));  // open: in_4, in_5, out_9, out_10, in_6, in_7, out_11, out_12
  // mem_main DMEM: pin names not known; wires that end beside it: ALU_output, RegFile_read_data_2, CLOCK, MemRW, out_12
  Bit_Extender #(.in_width(32), .out_width(2)) bit_extender_1 (.in(ALU_output), .out(bit_extender_1_out));
  Bit_Extender #(.in_width(32), .out_width(2)) bit_extender_2 (.in(ALU_output), .out(bit_extender_2_out));
  assign bit_extender_3_out = {{24{multiplexer_5_out[7]}}, multiplexer_5_out};  // Bit_Extender bit_extender_3
  Multiplexer #(.select(2), .width(8), .enable("false")) multiplexer_5 (
    .in0(out_12[7:0]), .in1(out_12[15:8]), .in2(out_12[23:16]), .in3(out_12[31:24]), .out(multiplexer_5_out),
    .sel(bit_extender_1_out));
  Multiplexer #(.select(2), .width(16), .enable("false")) multiplexer_6 (
    .in0(out_12[15:0]), .in1(out_12[23:8]), .in2(out_12[31:16]), .out(multiplexer_6_out),
    .sel(bit_extender_2_out));  // open: in3
  assign bit_extender_4_out = {{16{multiplexer_6_out[15]}}, multiplexer_6_out};  // Bit_Extender bit_extender_4
  Adder #(.width(32)) adder_2 (.a(PC_AfterReg), .b(32'h4), .out(adder_2_out));  // open: cin, cout
  Multiplexer #(.select(2), .width(32), .enable("false")) multiplexer_7 (
    .in0(multiplexer_8_out), .in1(ALU_output), .in2(adder_2_out), .out(WBValue), .sel(WBSel));  // open: in3
  Multiplexer #(.select(2), .width(32), .enable("false")) multiplexer_8 (
    .in0(bit_extender_3_out), .in1(bit_extender_4_out), .in2(out_12), .out(multiplexer_8_out),
    .sel(INSTRUCTION_AfterReg[13:12]));  // open: in3

  // Other names for the same wires on the sheet: clk = CLOCK; WriteAddress[31:0] = ALU_output

  // Notes on the sheet:
  //   Output
  //   IMEM (do **NOT** move this)
  //   Inputs
  //   It is OK to move the PC, RegFile, ALU, MEM, Branch Comp, Imm Gen, and Control Logic to wherever is most convenient for you when constructing your CPU, and to delete this text
  //   Inputs/Outputs for testing. Do **NOT** move these.
endmodule
