// Logisim project imm_gen.circ as structural Verilog: 1 circuit, main circuit imm_gen
module imm_gen (
  input  [31:0] inst,
  input  [2:0] ImmSel,
  output [31:0] imm
);

  wire [11:0] adder_1_out, bit_extender_1_out, bit_extender_2_out, shifter_1_out;
  wire [31:0] imm_I, imm_S, imm_SB, imm_UJ;

  assign bit_extender_1_out = {{7{1'b0}}, inst[11:7]};  // Bit_Extender bit_extender_1
  assign bit_extender_2_out = {{5{1'b0}}, inst[31:25]};  // Bit_Extender bit_extender_2
  Shifter #(.width(12)) shifter_1 (.in(bit_extender_2_out), .\dist (4'b0101), .out(shifter_1_out));
  assign imm_I = {{20{inst[31]}}, inst[31:20]};  // Bit_Extender bit_extender_3
  Adder #(.width(12)) adder_1 (.a(bit_extender_1_out), .b(shifter_1_out), .out(adder_1_out));  // open: cin, cout
  assign imm_S = {{20{adder_1_out[11]}}, adder_1_out};  // Bit_Extender bit_extender_4
  assign imm_S = {{20{inst[31]}}, {inst[31:25], inst[11:7]}};  // Bit_Extender bit_extender_5
  assign imm_SB = {{19{inst[31]}}, {inst[31], inst[7], inst[30:25], inst[11:8], 1'b0}};  // Bit_Extender bit_extender_6
  assign imm_UJ = {{11{inst[31]}}, {inst[31], inst[19:12], inst[20], inst[30:21], 1'b0}};  // Bit_Extender bit_extender_7
  Multiplexer #(.select(3), .width(32), .enable("false")) multiplexer_1 (
    .in0(imm_I), .in1(imm_S), .in2(imm_SB), .in3({inst[31:12], {12{1'b0}}}), .in4(imm_UJ), .out(imm),
    .sel(ImmSel));  // open: in5, in6, in7

  // Other names for the same wires on the sheet: imm_U[31:12] = inst[31:12]

  // Notes on the sheet:
  //   INPUTS to your circuit
  //   DON'T CHANGE THE LOCATIONS OF THE INPUTS AND OUTPUTS!
  //   OUTPUT from your circuit
endmodule
